# Fritzing sketch SunRise (saved by Fritzing 0.9.4)
breadboards: 1

parts:
  C1 = Electrolytic Capacitor [capacitance=470µF voltage=16V package="100 mil [THT, electrolytic]"]
  5V = Power plug [part_number=2A]
  Q1 = Basic FET N-Channel [part_number=STP16NF06 package="TO220 [THT]"]
  L1 = Inductor [inductance=100µH part_number="RLB0914-101KL max 1A !" package="400 mil [THT]"]
  D1 = Rectifier Diode [part_number=1N5822 package="300 mil [THT]"]
  C2 = Electrolytic Capacitor [capacitance=220µF voltage=25V package="100 mil [THT, electrolytic]"]
  Part1 = Arduino Nano (Rev3.0)
  BT1 = Bluetooth HC-06u [package=THT]
  Part2 = Real Time Clock Module - DS1307 RTC Breakout Board
  LED_MATRIX = LEDs [part_number="10W 12V" package=led-1206]
  R1 = Resistor [tolerance=±5% resistance=1k package=THT]
  R2 = Resistor [tolerance=±5% resistance=2k package=THT]

nets:
  GND: C1.-, 5V.GND, Q1.source, C2.-, Part1.GND, BT1.GND, Part2.GND, LED_MATRIX.C, R2.Pin_1
  VCC: C1.+, 5V.VCC, L1.pin_0, Part1.5V, BT1.VCC, Part2.5V
  N1: Q1.gate, Part1.D3
  N2: Q1.drain, L1.pin_1, D1.anode
  N3: D1.cathode, C2.+, LED_MATRIX.A
  N4: Part1.D1/TX, R1.Pin_0
  N5: Part1.D0/RX, BT1.TXD
  N6: Part1.A5, Part2.SCL
  N7: Part1.A4, Part2.SDA
  N8: BT1.RXD, R1.Pin_1, R2.Pin_0

custom parts:
  Bluetooth HC-06u: Bluetooth HC-06 - face up, pins down 16.5mm x 37.5mm PCB
